# Fritzing sketch grover (saved by Fritzing 0.9.3b)

parts:
  Power_plug1 = Power plug  # not connected
  Q1 = MOSFET-NCHANNEL [package=to220v]
  Q2 = MOSFET-NCHANNEL [package=to220v]  # not connected
  Q3 = MOSFET-NCHANNEL [package=to220v]  # not connected
  Q4 = MOSFET-NCHANNEL [package=to220v]
  Q5 = MOSFET-NCHANNEL [package=to220v]  # not connected
  Q6 = MOSFET-NCHANNEL [package=to220v]  # not connected
  M1 = DC Motor  # not connected
  M2 = DC Motor  # not connected
  M3 = DC Motor
  M4 = DC Motor  # not connected
  M5 = DC Motor  # not connected
  DS1 = DS18B20 1-Wire Temperature Sensor [part_number=DS18B20]  # not connected
  DS2 = DS18B20 1-Wire Temperature Sensor [part_number=DS18B20]  # not connected
  DS3 = DS18B20 1-Wire Temperature Sensor [part_number=DS18B20]  # not connected
  DS4 = DS18B20 1-Wire Temperature Sensor [part_number=DS18B20]  # not connected
  Conductivity_Circuit1 = Conductivity Circuit  # not connected
  Conductivity_Circuit2 = Conductivity Circuit  # not connected
  Conductivity_Circuit3 = Conductivity Circuit  # not connected
  Conductivity_Circuit4 = Conductivity Circuit  # not connected
  pH_Circuit1 = pH Circuit  # not connected
  pH_Circuit2 = pH Circuit  # not connected
  pH_Circuit3 = pH Circuit  # not connected
  pH_Circuit4 = pH Circuit  # not connected
  Raspberry_Pi_1 = Raspberry Pi 3 [part_number=RPI-3-V1.2]
  M6 = DC Motor

nets:
  N1: Q1.G, Raspberry_Pi_1.GIPO14
  N2: Q1.D, M6.pin_2
  N3: Q1.S, M6.pin_1
  N4: Q4.G, Raspberry_Pi_1.GIPO15
  N5: Q4.D, M3.pin_2
  N6: Q4.S, M3.pin_1
